// Logisim project DCNN.circ as structural Verilog
module main (
  input  Rst,
  input  Start,
  input  Clk,
  input  Stride,
  input  Filter_Size,
  input  Instr,
  output Done
);

  wire alu_1_byte, controller_1_en_alu, controller_1_en_dma, dma_1_en_cache, dma_1_en_ram, dma_1_r_w_cache,
       dma_1_r_w_ram, dma_1_read_filter;
  wire [1:0] controller_1_ctrl;
  wire [2:0] dma_1_cahce_row;
  wire [4:0] ram_1_data_out;
  wire [7:0] dma_1_cache_col;
  wire [17:0] dma_1_ram_addr;
  wire [24:0] filter_cache_1_filter, img_cache_1_cache_out;

  DMA dma_1 (
    .Reset(Rst), .En(controller_1_en_dma), .Clk(Clk), .Stride(Stride), .Filt_Sz(Filter_Size),
    .Ctrl(controller_1_ctrl), .En_Ram(dma_1_en_ram), .R_W_Ram(dma_1_r_w_ram), .Ram_Addr(dma_1_ram_addr),
    .En_Cache(dma_1_en_cache), .R_W_Cache(dma_1_r_w_cache), .Cahce_Row(dma_1_cahce_row),
    .Cache_Col(dma_1_cache_col), .Read_Filter(dma_1_read_filter), .Done(Done));
  Controller controller_1 (
    .Rst(Rst), .Clk(Clk), .Start(Start), .Done(Done), .Ctrl(controller_1_ctrl), .En_DMA(controller_1_en_dma),
    .En_ALU(controller_1_en_alu));
  Filter_Cache filter_cache_1 (
    .Rst(Rst), .Clk(Clk), .En(dma_1_read_filter), .Size(Filter_Size), .Data_In(ram_1_data_out),
    .Filter(filter_cache_1_filter));
  ALU alu_1 (
    .Rst(Rst), .Clk(Clk), .En(controller_1_en_alu), .Window(img_cache_1_cache_out),
    .Filter(filter_cache_1_filter), .Instr(Instr), .Byte(alu_1_byte));
  Ram ram_1 (
    .Rst(Rst), .Clk(Clk), .En(dma_1_en_ram), .R_W(dma_1_r_w_ram), .Addr(dma_1_ram_addr),
    .Data_In(alu_1_byte), .Data_Out(ram_1_data_out));
  Img_Cache img_cache_1 (
    .Rst(Rst), .Clk(Clk), .En(dma_1_en_cache), .R_W(dma_1_r_w_cache), .Row(dma_1_cahce_row),
    .Col(dma_1_cache_col), .Cache_In(ram_1_data_out), .Cache_Out(img_cache_1_cache_out));
endmodule

module DMA (
  input  Reset,
  input  En,
  input  Clk,
  input  Stride,
  input  Filt_Sz,
  input  [1:0] Ctrl,
  output En_Ram,
  output R_W_Ram,
  output [17:0] Ram_Addr,
  output En_Cache,
  output R_W_Cache,
  output [2:0] Cahce_Row,
  output [7:0] Cache_Col,
  output Read_Filter,
  output Done
);
endmodule

module Img_Cache (
  input  Rst,
  input  Clk,
  input  En,
  input  R_W,
  input  [2:0] Row,
  input  [7:0] Col,
  input  [4:0] Cache_In,
  output [24:0] Cache_Out
);
endmodule

module Controller (
  input  Rst,
  input  Clk,
  input  Start,
  input  Done,
  output [1:0] Ctrl,
  output En_DMA,
  output En_ALU
);
endmodule

module ALU (
  input  Rst,
  input  Clk,
  input  En,
  input  [24:0] Window,
  input  [24:0] Filter,
  input  Instr,
  output Byte
);

  wire [16:0] undriven, undriven_2, undriven_3;

  ALU_Buffer alu_buffer_1 (
    .A_In(undriven_3), .S_In(undriven_2), .P_In(undriven), .Rst(Rst), .Clk(Clk), .En(En));  // open: A_Out, S_Out, P_Out
  ALU_Stage_Unit alu_stage_unit_1 ();  // open: A_In, S_In, P_In, A_Out, S_Out, P_Out
endmodule

module Ram (
  input  Rst,
  input  Clk,
  input  En,
  input  R_W,
  input  [17:0] Addr,
  input  Data_In,
  output [4:0] Data_Out
);
endmodule

// +
module ALU_Buffer (
  input  [16:0] A_In,
  input  [16:0] S_In,
  input  [16:0] P_In,
  input  Rst,
  input  Clk,
  input  En,
  output [16:0] A_Out,
  output [16:0] S_Out,
  output [16:0] P_Out
);

  Register #(.width(17)) A_Reg (.D(A_In), .en(En), .clk(Clk), .Q(A_Out), .clr(Rst));
  Register #(.width(17)) S_Reg (.D(S_In), .en(En), .clk(Clk), .Q(S_Out), .clr(Rst));
  Register #(.width(17)) P_Reg (.D(P_In), .en(En), .clk(Clk), .Q(P_Out), .clr(Rst));
endmodule

module ALU_Stage_Unit (
  input  [16:0] A_In,
  input  [16:0] S_In,
  input  [16:0] P_In,
  output [16:0] A_Out,
  output [16:0] S_Out,
  output [16:0] P_Out
);

  wire [0:0] adder_1_out;
  wire [16:0] multiplexer_1_out;

  Multiplexer #(.select(2), .width(17), .enable("false")) multiplexer_1 (
    .in0({17{1'b0}}), .in1(A_In), .in2(S_In), .in3({17{1'b0}}), .out(multiplexer_1_out));  // open: sel
  Adder #(.width(17)) adder_1 (
    .a(multiplexer_1_out), .b(P_In), .out({P_Out[1], P_Out[16:2], adder_1_out[0]}));  // open: cin, cout

  assign A_Out = A_In;
  assign P_Out[0] = P_Out[1];
  assign S_Out = S_In;
endmodule

module Filter_Cache (
  input  Rst,
  input  Clk,
  input  En,
  input  Size,
  input  [4:0] Data_In,
  output [24:0] Filter
);
endmodule
